// Logisim project General Purpose Processor.circ as structural Verilog: 8 circuits, main circuit main
module main (
);

  wire clock_1_out, cpu_1_output_show, cpu_1_ram_clear, cpu_1_ram_load, cpu_1_ram_store,
       cpu_1_user_input_read, RESET_out;
  wire [6:0] keyboard_1_data;
  wire [7:0] cpu_1_output_data, cpu_1_ram_data_write, ram_1_data, register_1_q, rom_1_data;
  wire [7:7] keyboard_1_avail;
  wire [15:0] cpu_1_ram_address, cpu_1_rom_address;

  Clock clock_1 (.out(clock_1_out));
  Button RESET (.out(RESET_out));
  Keyboard keyboard_1 (
    .clk(clock_1_out), .re(cpu_1_user_input_read), .clr(RESET_out), .avail(keyboard_1_avail[7]),
    .data(keyboard_1_data));
  ROM #(.addrWidth(16)) rom_1 (.addr(cpu_1_rom_address), .data(rom_1_data), .sel(1'b1));
  // Probe on cpu_1_output_data
  CPU cpu_1 (
    .RESET_high(RESET_out), .ROM_address(cpu_1_rom_address), .ROM_data(rom_1_data), .Clock(clock_1_out),
    .GND(1'b0), .Output_data(cpu_1_output_data), .RAM_data_read(ram_1_data),
    .RAM_data_write(cpu_1_ram_data_write), .RAM_address(cpu_1_ram_address), .RAM_store(cpu_1_ram_store),
    .RAM_load(cpu_1_ram_load), .RAM_clear(cpu_1_ram_clear), .VCC(1'b1), .Output_Show(cpu_1_output_show),
    .User_Input_Bus({keyboard_1_avail[7], keyboard_1_data}), .User_Input_read(cpu_1_user_input_read));
  Register register_1 (
    .D(cpu_1_output_data), .en(cpu_1_output_show), .Q(register_1_q), .clk(clock_1_out), .clr(RESET_out));
  // Probe on register_1_q
  Hex_Digit_Display hex_digit_display_1 (.value(register_1_q[7:4]));  // open: dp
  TTY tty_1 (.data(cpu_1_output_data[6:0]), .clk(clock_1_out), .we(cpu_1_output_show), .clr(RESET_out));
  RAM #(.addrWidth(16), .bus("separate")) ram_1 (
    .addr(cpu_1_ram_address), .din(cpu_1_ram_data_write), .data(ram_1_data), .str(cpu_1_ram_store),
    .sel(1'b1), .clk(clock_1_out), .ld(cpu_1_ram_load), .clr(cpu_1_ram_clear));
  Hex_Digit_Display hex_digit_display_2 (.value(register_1_q[3:0]));  // open: dp
  Counter counter_1 (.count(cpu_1_output_show), .clk(clock_1_out), .clr(RESET_out));  // open: load, D, Q, carry

  // Notes on the sheet:
  //   contents of rom_1 (hex, n*v repeats v):
  //   2 90 2 9 1 16 2 bc 1 0 2 bd 3 0 6 4 1 0 2 bc 5 0 2 b 4 0 1 0 2 bc 2 bd 5
endmodule

module CPU (
  input  [7:0] ROM_data,
  input  Clock,
  input  RESET_high,
  input  [7:0] RAM_data_read,
  input  GND,
  input  VCC,
  input  [7:0] User_Input_Bus,
  output [15:0] ROM_address,
  output [7:0] RAM_data_write,
  output [15:0] RAM_address,
  output RAM_store,
  output RAM_load,
  output RAM_clear,
  output [7:0] Output_data,
  output Output_Show,
  output User_Input_read
);

  wire and_1_out, control_unit_1_alu_compute, control_unit_1_branch, control_unit_1_get_prog_ctr,
       control_unit_1_input_write, control_unit_1_jump, control_unit_1_transfer,
       instruction_decoder_1_increment, multiplexer_1_out, or_1_out, or_2_out, transfer_controller_1_show,
       transfer_controller_1_show_2, transfer_controller_1_write_enabl_5, transfer_controller_1_write_enable,
       transfer_controller_1_write_enable_1, transfer_controller_1_write_enable_2,
       transfer_controller_1_write_enable_3, transfer_controller_1_write_enable_4;
  wire [2:0] instruction_decoder_1_operand, transfer_controller_1_from_addr_gpr,
       transfer_controller_1_to_addr_gpr;
  wire [5:0] alu_1_overflow;
  wire [7:0] A_q, alu_1_output, B_q, GP_Reg_data_out, instruction_decoder_1_operation,
       Internal_Input_Register_q, Output_Buffer_q, register_1_q, Result_q, shift_register_1_out,
       shift_register_1_q0, shift_register_1_q1, transfer_controller_1_data2, transfer_controller_1_data_1_2,
       transfer_controller_1_data_3_2, transfer_controller_1_data_4_2, transfer_controller_1_data_5_2,
       transfer_controller_1_data_8;
  wire [7:3] instruction_decoder_1_operand_2;
  wire [15:0] adder_1_out, controlled_buffer_2_out, subtractor_1_out;

  Multiplexer #(.select(3), .disabled(0)) multiplexer_1 (
    .in0(alu_1_overflow[0]), .in1(alu_1_overflow[1]), .in2(alu_1_overflow[2]), .in3(alu_1_overflow[3]),
    .in4(alu_1_overflow[4]), .in5(alu_1_overflow[5]), .out(multiplexer_1_out),
    .sel(instruction_decoder_1_operand), .en(control_unit_1_branch));  // open: in6, in7
  Register A (
    .D(transfer_controller_1_data_1_2), .en(transfer_controller_1_write_enable_1), .Q(A_q), .clk(Clock),
    .clr(GND));
  Register B (
    .D(transfer_controller_1_data2), .en(transfer_controller_1_write_enable_2), .Q(B_q), .clk(Clock),
    .clr(GND));
  Instruction_Decoder instruction_decoder_1 (
    .should_Branch(multiplexer_1_out), .Clock(Clock), .Data_input(ROM_data), .Reset(RESET_high),
    .Increment(instruction_decoder_1_increment), .operation(instruction_decoder_1_operation),
    .operand({instruction_decoder_1_operand_2, instruction_decoder_1_operand}));
  Register Result (.D(alu_1_output), .en(control_unit_1_alu_compute), .Q(Result_q), .clk(Clock), .clr(GND));
  ALU alu_1 (
    .Enable(control_unit_1_alu_compute), .Instruction(instruction_decoder_1_operand), .Input_A(A_q),
    .Input_B(B_q), .Output(alu_1_output), .isZero(alu_1_overflow[5]), .Negative(alu_1_overflow[4]),
    .A_B(alu_1_overflow[3]), .A_B_2(alu_1_overflow[2]), .A_B_3(alu_1_overflow[1]),
    .Overflow(alu_1_overflow[0]), .Clock(Clock), .Reset(RESET_high));
  Control_Unit control_unit_1 (
    .Operation(instruction_decoder_1_operation), .Input_write(control_unit_1_input_write),
    .Transfer(control_unit_1_transfer), .ALU_compute(control_unit_1_alu_compute), .Output_show(Output_Show),
    .Jump(control_unit_1_jump), .Branch(control_unit_1_branch), .Get_Prog_Ctr(control_unit_1_get_prog_ctr));
  Register Internal_Input_Register (
    .D({instruction_decoder_1_operand_2, instruction_decoder_1_operand}), .en(control_unit_1_input_write),
    .Q(Internal_Input_Register_q), .clk(Clock), .clr(GND));
  Register register_1 (.D(User_Input_Bus), .en(VCC), .Q(register_1_q), .clk(Clock), .clr(GND));
  GP_Registers GP_Reg (
    .Data_Out(GP_Reg_data_out), .Data_in(transfer_controller_1_data_8),
    .Write_address(transfer_controller_1_to_addr_gpr), .Write_enable(transfer_controller_1_write_enable),
    .Clock(Clock), .Address_out(transfer_controller_1_from_addr_gpr), .Show(transfer_controller_1_show));
  Transfer_Controller transfer_controller_1 (
    .Enable(control_unit_1_transfer), .From(instruction_decoder_1_operand_2[7:4]),
    .To({instruction_decoder_1_operand_2[3], instruction_decoder_1_operand}), .Data(GP_Reg_data_out),
    .Show(transfer_controller_1_show), .Data_0(Result_q), .Data_1(register_1_q), .Show_1(User_Input_read),
    .Data_2(shift_register_1_out), .Show_2(transfer_controller_1_show_2), .Data_3(Internal_Input_Register_q),
    .Data_4(RAM_address[7:0]), .Data_5(RAM_address[15:8]), .Data_6(RAM_data_read), .Show_6(RAM_load),
    .From_Addr_GPR(transfer_controller_1_from_addr_gpr), .To_Addr_GPR(transfer_controller_1_to_addr_gpr),
    .Data_8(transfer_controller_1_data_8), .Write_enable(transfer_controller_1_write_enable),
    .Data_1_2(transfer_controller_1_data_1_2), .Write_enable_1(transfer_controller_1_write_enable_1),
    .Data2(transfer_controller_1_data2), .Write_enable_2(transfer_controller_1_write_enable_2),
    .Data_3_2(transfer_controller_1_data_3_2), .Write_enable_3(transfer_controller_1_write_enable_3),
    .Data_4_2(transfer_controller_1_data_4_2), .Write_enable_4(transfer_controller_1_write_enable_4),
    .Data_5_2(transfer_controller_1_data_5_2), .Write_enabl_5(transfer_controller_1_write_enabl_5),
    .Data_6_2(RAM_data_write), .Write_enable_6(RAM_store));  // open: Show_0, Show_3, Show_4, Show_5, Data_7, Show_7, Data_0_2, Write_enable_0, Data_7_2, Write_enable_7
  Register register_2 (
    .D(transfer_controller_1_data_4_2), .en(transfer_controller_1_write_enable_4), .Q(RAM_address[7:0]),
    .clk(Clock), .clr(GND));
  Register register_3 (
    .D(transfer_controller_1_data_5_2), .en(transfer_controller_1_write_enabl_5), .Q(RAM_address[15:8]),
    .clk(Clock), .clr(GND));
  assign Output_data = Output_Show ? Output_Buffer_q : 8'bz;  // Controlled_Buffer controlled_buffer_1
  Register Output_Buffer (
    .D(transfer_controller_1_data_3_2), .en(transfer_controller_1_write_enable_3), .Q(Output_Buffer_q),
    .clk(Clock), .clr(GND));
  or or_1 (or_1_out, multiplexer_1_out, control_unit_1_jump);
  assign controlled_buffer_2_out = or_1_out ? RAM_address : 16'bz;  // Controlled_Buffer controlled_buffer_2
  or or_2 (or_2_out, or_1_out, instruction_decoder_1_increment);
  Register #(.width(16)) Prog_Pointer (
    .D(controlled_buffer_2_out), .en(or_2_out), .Q(ROM_address), .clk(Clock), .clr(RESET_high));
  and and_1 (and_1_out, ~or_1_out, instruction_decoder_1_increment);  // AND_Gate
  assign controlled_buffer_2_out = and_1_out ? adder_1_out : 16'bz;  // Controlled_Buffer controlled_buffer_3
  Adder #(.width(16)) adder_1 (.a(ROM_address), .b(16'h1), .out(adder_1_out));  // open: cin, cout
  Subtractor #(.width(16)) subtractor_1 (.a(ROM_address), .b(16'h1), .out(subtractor_1_out));  // open: bin, bout
  Shift_Register #(.width(8), .length(2)) shift_register_1 (
    .shift(transfer_controller_1_show_2), .clk(Clock), .out(shift_register_1_out),
    .load(control_unit_1_get_prog_ctr), .clr(RESET_high), .d0(subtractor_1_out[15:8]),
    .q0(shift_register_1_q0), .d1(subtractor_1_out[7:0]), .q1(shift_register_1_q1));  // open: in
  // Probe on shift_register_1_q0
  // Probe on shift_register_1_q1
  // Probe on shift_register_1_out
  Register #(.width(16)) register_4 ();  // open: D, en, Q, clk, clr

  assign RAM_clear = RESET_high;
endmodule

module GP_Register_Bank__3_bit_addr (
  input  [7:0] Data_in,
  input  [2:0] Address_in,
  input  Write_enable,
  input  Clock,
  input  Output_enable,
  input  [2:0] Address_out,
  output [7:0] Data_out
);

  wire decoder_1_out0, decoder_1_out1, decoder_1_out2, decoder_1_out3, decoder_1_out4, decoder_1_out5,
       decoder_1_out6, decoder_1_out7;
  wire [7:0] demultiplexer_1_out0, demultiplexer_1_out1, demultiplexer_1_out2, demultiplexer_1_out3,
       demultiplexer_1_out4, demultiplexer_1_out5, demultiplexer_1_out6, demultiplexer_1_out7, register_1_q,
       register_2_q, register_3_q, register_4_q, register_5_q, register_6_q, register_7_q, register_8_q;

  Demultiplexer #(.select(3), .width(8)) demultiplexer_1 (
    .out0(demultiplexer_1_out0), .out1(demultiplexer_1_out1), .out2(demultiplexer_1_out2),
    .out3(demultiplexer_1_out3), .out4(demultiplexer_1_out4), .out5(demultiplexer_1_out5),
    .out6(demultiplexer_1_out6), .out7(demultiplexer_1_out7), .in(Data_in), .sel(Address_in),
    .en(Write_enable));
  Decoder #(.select(3), .disabled(0)) decoder_1 (
    .out0(decoder_1_out0), .out1(decoder_1_out1), .out2(decoder_1_out2), .out3(decoder_1_out3),
    .out4(decoder_1_out4), .out5(decoder_1_out5), .out6(decoder_1_out6), .out7(decoder_1_out7),
    .sel(Address_in), .en(Write_enable));
  Register register_1 (.D(demultiplexer_1_out0), .en(decoder_1_out0), .Q(register_1_q), .clk(Clock), .clr(1'b0));
  Register register_2 (.D(demultiplexer_1_out1), .en(decoder_1_out1), .Q(register_2_q), .clk(Clock), .clr(1'b0));
  Register register_3 (.D(demultiplexer_1_out2), .en(decoder_1_out2), .Q(register_3_q), .clk(Clock), .clr(1'b0));
  Register register_4 (.D(demultiplexer_1_out3), .en(decoder_1_out3), .Q(register_4_q), .clk(Clock), .clr(1'b0));
  Register register_5 (.D(demultiplexer_1_out4), .en(decoder_1_out4), .Q(register_5_q), .clk(Clock), .clr(1'b0));
  Register register_6 (.D(demultiplexer_1_out5), .en(decoder_1_out5), .Q(register_6_q), .clk(Clock), .clr(1'b0));
  Register register_7 (.D(demultiplexer_1_out6), .en(decoder_1_out6), .Q(register_7_q), .clk(Clock), .clr(1'b0));
  Register register_8 (.D(demultiplexer_1_out7), .en(decoder_1_out7), .Q(register_8_q), .clk(Clock), .clr(1'b0));
  Multiplexer #(.select(3), .width(8)) multiplexer_1 (
    .in0(register_1_q), .in1(register_2_q), .in2(register_3_q), .in3(register_4_q), .in4(register_5_q),
    .in5(register_6_q), .in6(register_7_q), .in7(register_8_q), .out(Data_out), .sel(Address_out),
    .en(Output_enable));
endmodule

module GP_Registers (
  input  [7:0] Data_in,
  input  [2:0] Write_address,
  input  Write_enable,
  input  Clock,
  input  [2:0] Address_out,
  input  Show,
  output [7:0] Data_Out
);

  wire [2:0] controlled_buffer_1_out, controlled_buffer_2_out;
  wire [7:0] controlled_buffer_3_out, gp_register_bank_3_bit_addr_1_data_out;

  assign controlled_buffer_1_out = Show ? Address_out : 3'bz;  // Controlled_Buffer controlled_buffer_1
  assign controlled_buffer_2_out = Write_enable ? Write_address : 3'bz;  // Controlled_Buffer controlled_buffer_2
  assign controlled_buffer_3_out = Write_enable ? Data_in : 8'bz;  // Controlled_Buffer controlled_buffer_3
  assign Data_Out = Show ? gp_register_bank_3_bit_addr_1_data_out : 8'bz;  // Controlled_Buffer controlled_buffer_4
  GP_Register_Bank__3_bit_addr gp_register_bank_3_bit_addr_1 (
    .Data_in(controlled_buffer_3_out), .Address_in(controlled_buffer_2_out), .Write_enable(Write_enable),
    .Output_enable(Show), .Address_out(controlled_buffer_1_out),
    .Data_out(gp_register_bank_3_bit_addr_1_data_out), .Clock(Clock));
endmodule

module ALU (
  input  Reset,
  input  Clock,
  input  Enable,
  input  [2:0] Instruction,
  input  [7:0] Input_A,
  input  [7:0] Input_B,
  output [7:0] Output,
  output isZero,
  output Negative,
  output A_B,
  output A_B_2,
  output A_B_3,
  output Overflow
);

  wire [6:0] register_1_q;
  wire [7:0] adder_1_out, divider_1_out, divider_1_rem, multiplexer_1_out, multiplier_1_out, negator_1_out,
       negator_2_out, subtractor_1_out;

  Adder adder_1 (.a(Input_A), .b(Input_B), .out(adder_1_out), .cout(Overflow));  // open: cin
  Subtractor subtractor_1 (.a(Input_A), .b(Input_B), .out(subtractor_1_out));  // open: bin, bout
  Multiplier multiplier_1 (.a(Input_A), .b(Input_B), .out(multiplier_1_out));  // open: cin, cout
  Divider divider_1 (.a(Input_A), .b(Input_B), .out(divider_1_out), .rem(divider_1_rem));  // open: upper
  Negator negator_1 (.in(Input_A), .out(negator_1_out));
  Negator negator_2 (.in(Input_B), .out(negator_2_out));
  Comparator comparator_1 (.a(Input_A), .b(Input_B), .gt(A_B), .eq(A_B_2), .lt(A_B_3));
  Multiplexer #(.select(3), .width(8)) multiplexer_1 (
    .in0(adder_1_out), .in1(subtractor_1_out), .in2(multiplier_1_out), .in3(divider_1_out),
    .in4(divider_1_rem), .in5(negator_1_out), .in6(negator_2_out), .out(multiplexer_1_out),
    .sel(Instruction), .en(Enable));  // open: in7
  Register register_1 (.D(multiplexer_1_out), .en(Enable), .Q({Negative, register_1_q}), .clk(Clock), .clr(Reset));
  nand nand_1 (isZero, register_1_q[0], register_1_q[1], register_1_q[2], register_1_q[3], register_1_q[4], register_1_q[5], register_1_q[6], Negative);
  assign Output = Enable ? multiplexer_1_out : 8'bz;  // Controlled_Buffer controlled_buffer_1
endmodule

module Transfer_Controller (
  input  Enable,
  input  [3:0] From,
  input  [3:0] To,
  input  [7:0] Data,
  input  [7:0] Data_0,
  input  [7:0] Data_1,
  input  [7:0] Data_2,
  input  [7:0] Data_3,
  input  [7:0] Data_4,
  input  [7:0] Data_5,
  input  [7:0] Data_6,
  input  [7:0] Data_7,
  output [2:0] From_Addr_GPR,
  output [2:0] To_Addr_GPR,
  output [7:0] Data_8,
  output Show,
  output Write_enable,
  output [7:0] Data_0_2,
  output Show_0,
  output Write_enable_0,
  output [7:0] Data_1_2,
  output Show_1,
  output Write_enable_1,
  output [7:0] Data2,
  output Show_2,
  output Write_enable_2,
  output [7:0] Data_3_2,
  output Show_3,
  output Write_enable_3,
  output [7:0] Data_4_2,
  output Show_4,
  output Write_enable_4,
  output [7:0] Data_5_2,
  output Show_5,
  output Write_enabl_5,
  output Show_6,
  output [7:0] Data_6_2,
  output Write_enable_6,
  output Show_7,
  output [7:0] Data_7_2,
  output Write_enable_7
);

  wire and_1_out, and_2_out, decoder_1_out0, decoder_1_out1, decoder_1_out2, decoder_1_out3, decoder_1_out4,
       decoder_1_out5, decoder_1_out6, decoder_1_out7, decoder_2_out0, decoder_2_out1, decoder_2_out2,
       decoder_2_out3, decoder_2_out4, decoder_2_out5, decoder_2_out6, decoder_2_out7, not_1_out, not_2_out,
       or_1_out, or_2_out, or_3_out, or_4_out, or_5_out, or_6_out, or_7_out, or_8_out, or_9_out, or_10_out;
  wire [7:0] multiplexer_1_out;

  Decoder #(.select(4), .disabled(0)) decoder_1 (
    .out0(decoder_1_out0), .out1(decoder_1_out1), .out2(decoder_1_out2), .out3(decoder_1_out3),
    .out4(decoder_1_out4), .out5(decoder_1_out5), .out6(decoder_1_out6), .out7(decoder_1_out7),
    .out8(Show_0), .out9(Show_1), .out10(Show_2), .out11(Show_3), .out12(Show_4), .out13(Show_5),
    .out14(Show_6), .out15(Show_7), .sel(From), .en(Enable));
  or or_1 (or_1_out, decoder_1_out0, decoder_1_out1, decoder_1_out2);
  or or_2 (or_2_out, or_1_out, decoder_1_out3);
  or or_3 (or_3_out, decoder_1_out4, or_4_out);
  or or_4 (or_4_out, decoder_1_out5, decoder_1_out6, decoder_1_out7);
  or or_5 (or_5_out, or_2_out, or_3_out);
  assign Show = Enable ? or_5_out : 1'bz;  // Controlled_Buffer controlled_buffer_1
  Pull_Resistor pull_resistor_1 (.node(Show));
  Multiplexer #(.select(4), .width(8)) multiplexer_1 (
    .in0(Data), .in1(Data), .in2(Data), .in3(Data), .in4(Data), .in5(Data), .in6(Data), .in7(Data),
    .in8(Data_0), .in9(Data_1), .in10(Data_2), .in11(Data_3), .in12(Data_4), .in13(Data_5), .in14(Data_6),
    .in15(Data_7), .out(multiplexer_1_out), .sel(From), .en(Enable));
  Demultiplexer #(.select(4), .width(8), .tristate("true"), .disabled(0)) demultiplexer_1 (
    .out0(Data_8), .out1(Data_8), .out2(Data_8), .out3(Data_8), .out4(Data_8), .out5(Data_8), .out6(Data_8),
    .out7(Data_8), .out8(Data_0_2), .out9(Data_1_2), .out10(Data2), .out11(Data_3_2), .out12(Data_4_2),
    .out13(Data_5_2), .out14(Data_6_2), .out15(Data_7_2), .in(multiplexer_1_out), .sel(To), .en(Enable));
  not not_1 (not_1_out, From[3]);
  not not_2 (not_2_out, To[3]);
  Decoder #(.select(4), .disabled(0)) decoder_2 (
    .out0(decoder_2_out0), .out1(decoder_2_out1), .out2(decoder_2_out2), .out3(decoder_2_out3),
    .out4(decoder_2_out4), .out5(decoder_2_out5), .out6(decoder_2_out6), .out7(decoder_2_out7),
    .out8(Write_enable_0), .out9(Write_enable_1), .out10(Write_enable_2), .out11(Write_enable_3),
    .out12(Write_enable_4), .out13(Write_enabl_5), .out14(Write_enable_6), .out15(Write_enable_7), .sel(To),
    .en(Enable));
  and and_1 (and_1_out, not_1_out, Enable);
  and and_2 (and_2_out, not_2_out, Enable);
  or or_6 (or_6_out, decoder_2_out0, decoder_2_out1, decoder_2_out2);
  or or_7 (or_7_out, or_6_out, decoder_2_out3);
  or or_8 (or_8_out, decoder_2_out4, or_9_out);
  or or_9 (or_9_out, decoder_2_out5, decoder_2_out6, decoder_2_out7);
  assign From_Addr_GPR = and_1_out ? From[2:0] : 3'bz;  // Controlled_Buffer controlled_buffer_2
  assign To_Addr_GPR = and_2_out ? To[2:0] : 3'bz;  // Controlled_Buffer controlled_buffer_3
  or or_10 (or_10_out, or_7_out, or_8_out);
  assign Write_enable = Enable ? or_10_out : 1'bz;  // Controlled_Buffer controlled_buffer_4
  Pull_Resistor pull_resistor_2 (.node(Write_enable));
endmodule

module Control_Unit (
  input  [7:0] Operation,
  output Input_write,
  output Transfer,
  output ALU_compute,
  output Output_show,
  output Jump,
  output Branch,
  output Get_Prog_Ctr
);

  wire decoder_1_out0, decoder_1_out8, decoder_1_out9, decoder_1_out10, decoder_1_out11, decoder_1_out12,
       decoder_1_out13, decoder_1_out14, decoder_1_out15, pull_resistor_1_node;

  Pull_Resistor #(.pull(1)) pull_resistor_1 (.node(pull_resistor_1_node));
  Decoder #(.select(4)) decoder_1 (
    .out0(decoder_1_out0), .out1(Input_write), .out2(Transfer), .out3(ALU_compute), .out4(Output_show),
    .out5(Jump), .out6(Branch), .out7(Get_Prog_Ctr), .out8(decoder_1_out8), .out9(decoder_1_out9),
    .out10(decoder_1_out10), .out11(decoder_1_out11), .out12(decoder_1_out12), .out13(decoder_1_out13),
    .out14(decoder_1_out14), .out15(decoder_1_out15), .sel(Operation[3:0]), .en(pull_resistor_1_node));
endmodule

// IU
module Instruction_Decoder (
  input  should_Branch,
  input  Clock,
  input  [7:0] Data_input,
  input  Reset,
  output Increment,
  output [7:0] operation,
  output [7:0] operand
);

  wire and_1_out, and_2_out, and_3_out, comparator_1_eq, comparator_2_eq, not_1_out, not_2_out, or_1_out,
       or_3_out, shift_register_1_out, shift_register_1_q0, shift_register_1_q1, shift_register_1_q2,
       shift_register_1_q3;
  wire [7:0] register_1_q, register_2_q;

  not not_1 (not_1_out, or_1_out);
  Shift_Register #(.length(4)) shift_register_1 (
    .shift(not_1_out), .in(shift_register_1_out), .clk(Clock), .out(shift_register_1_out), .load(or_1_out),
    .clr(Reset), .d0(1'b1), .q0(shift_register_1_q0), .d1(not_2_out), .q1(shift_register_1_q1),
    .d2(not_2_out), .q2(shift_register_1_q2), .d3(not_2_out), .q3(shift_register_1_q3));
  Pull_Resistor pull_resistor_1 (.node(Reset));
  not not_2 (not_2_out, 1'b1);
  Register #(.trigger("high")) register_1 (
    .D(Data_input), .en(shift_register_1_q0), .Q(register_1_q), .clk(Clock), .clr(Reset));
  or or_1 (or_1_out, and_1_out, or_3_out);
  and and_1 (and_1_out, ~shift_register_1_q0, ~shift_register_1_q1, ~shift_register_1_q2, ~shift_register_1_q3);  // AND_Gate
  Register #(.trigger("high")) register_2 (
    .D(Data_input), .en(shift_register_1_q2), .Q(register_2_q), .clk(Clock), .clr(Reset));
  or or_2 (Increment, shift_register_1_q1, shift_register_1_q3);
  assign operation = shift_register_1_q2 ? register_1_q : 8'bz;  // Controlled_Buffer controlled_buffer_1
  assign operand = shift_register_1_q2 ? register_2_q : 8'bz;  // Controlled_Buffer controlled_buffer_2
  Pull_Resistor pull_resistor_2 (.node(operand));
  Pull_Resistor pull_resistor_3 (.node(operation));
  Comparator comparator_1 (.a(8'h6), .b(operation), .eq(comparator_1_eq));  // open: gt, lt
  or or_3 (or_3_out, and_3_out, comparator_2_eq);
  Comparator comparator_2 (.a(8'h5), .b(operation), .eq(comparator_2_eq));  // open: gt, lt
  and and_2 (and_2_out, shift_register_1_q2, comparator_1_eq);
  and and_3 (and_3_out, and_2_out, should_Branch);
endmodule
